# Fritzing sketch Sketch (saved by Fritzing 0.9.3b)
breadboards: 1

parts:
  R1 = Resistor [tolerance=±5% resistance=220 package=THT]
  LED1 = LED - 3mm [color="Red (633nm)" package="3 mm [THT]"]
  R2 = PHOTOCELL [package=photocell-kit]
  WeMos_D1_Mini1 = WeMos D1 Mini  # not connected
  R3 = Trimmer Potentiometer [maximum_resistance=10kΩ package=THT]
  WeMos_D1_Mini2 = WeMos D1 Mini  # not connected
  DHT1 = DHT11 Humitidy and Temperature Sensor  # not connected

nets:
  N1: R1.Pin_0, LED1.anode
  N2: R2.P$1, R3.wiper

custom parts:
  DHT11 Humitidy and Temperature Sensor: DHT11 Humidity and Temperature Sensor
